// Logisim project hack.circ as structural Verilog: 23 circuits, main circuit main
module main (
);

  wire button_1_out, clock_1_out, cpu_1_writem, switch_1_p2;
  wire [14:0] cpu_1_addressm, cpu_1_pc;
  wire [15:0] cpu_1_outm, instruction_memory_data, ram_1_dout;

  Button button_1 (.out(button_1_out));
  ROM #(.addrWidth(15), .dataWidth(16)) instruction_memory (.addr(cpu_1_pc), .data(instruction_memory_data));
  Clock clock_1 (.out(clock_1_out));
  // Switch switch_1: pin names not known; wires that end beside it: clock_1_out, switch_1_p2
  CPU cpu_1 (
    .instruction(instruction_memory_data), .inM(ram_1_dout), .reset(button_1_out), .clk(switch_1_p2),
    .outM(cpu_1_outm), .writeM(cpu_1_writem), .addressM(cpu_1_addressm), .pc(cpu_1_pc));
  RAM #(.addrWidth(15), .dataWidth(16)) ram_1 (
    .addr(cpu_1_addressm), .we(cpu_1_writem), .oe(1'b1), .clk(switch_1_p2), .din(cpu_1_outm),
    .dout(ram_1_dout));
endmodule

module half_adder (
  input  a,
  input  b,
  output carry,
  output sum
);

  and and_1 (carry, a, b);
  xor xor_1 (sum, a, b);
endmodule

module full_Adder (
  input  cin,
  input  a,
  input  b,
  output sum,
  output carry
);

  wire H1_carry, H1_sum, H2_carry;

  half_adder H1 (.a(a), .b(b), .carry(H1_carry), .sum(H1_sum));
  half_adder H2 (.a(cin), .b(H1_sum), .carry(H2_carry), .sum(sum));
  or or_1 (carry, H1_carry, H2_carry);
endmodule

module add16 (
  input  [15:0] A,
  input  [15:0] B,
  output [15:0] sum,
  output carry
);

  wire add0_carry, add1_carry, add2_carry, add3_carry, add4_carry, add5_carry, add6_carry, add7_carry,
       add8_carry, add9_carry, add10_carry, add11_carry, add12_carry, add13_carry, add14_carry;

  full_Adder add0 (.a(A[0]), .b(B[0]), .sum(sum[0]), .carry(add0_carry));  // open: cin
  full_Adder add1 (.cin(add0_carry), .a(A[1]), .b(B[1]), .sum(sum[1]), .carry(add1_carry));
  full_Adder add2 (.cin(add1_carry), .a(A[2]), .b(B[2]), .sum(sum[2]), .carry(add2_carry));
  full_Adder add3 (.cin(add2_carry), .a(A[3]), .b(B[3]), .sum(sum[3]), .carry(add3_carry));
  full_Adder add4 (.cin(add3_carry), .a(A[4]), .b(B[4]), .sum(sum[4]), .carry(add4_carry));
  full_Adder add5 (.cin(add4_carry), .a(A[5]), .b(B[5]), .sum(sum[5]), .carry(add5_carry));
  full_Adder add6 (.cin(add5_carry), .a(A[6]), .b(B[6]), .sum(sum[6]), .carry(add6_carry));
  full_Adder add7 (.cin(add6_carry), .a(A[7]), .b(B[7]), .sum(sum[7]), .carry(add7_carry));
  full_Adder add8 (.cin(add7_carry), .a(A[8]), .b(B[8]), .sum(sum[8]), .carry(add8_carry));
  full_Adder add9 (.cin(add8_carry), .a(A[9]), .b(B[9]), .sum(sum[9]), .carry(add9_carry));
  full_Adder add10 (.cin(add9_carry), .a(A[10]), .b(B[10]), .sum(sum[10]), .carry(add10_carry));
  full_Adder add11 (.cin(add10_carry), .a(A[11]), .b(B[11]), .sum(sum[11]), .carry(add11_carry));
  full_Adder add12 (.cin(add11_carry), .a(A[12]), .b(B[12]), .sum(sum[12]), .carry(add12_carry));
  full_Adder add13 (.cin(add12_carry), .a(A[13]), .b(B[13]), .sum(sum[13]), .carry(add13_carry));
  full_Adder add14 (.cin(add13_carry), .a(A[14]), .b(B[14]), .sum(sum[14]), .carry(add14_carry));
  full_Adder add15 (.cin(add14_carry), .a(A[15]), .b(B[15]), .sum(sum[15]), .carry(carry));
endmodule

module ALU (
  input  [15:0] X,
  input  zero_x,
  input  negate_x,
  input  [15:0] Y,
  input  zero_y,
  input  negate_y,
  input  add_and,
  input  negate_out,
  output [15:0] alu_out,
  output carry
);

  wire [15:0] add16_1_sum, and_1_out, multiplexer_1_out, multiplexer_2_out, multiplexer_3_out,
       multiplexer_4_out, multiplexer_5_out, not_1_out, not_2_out, not_3_out;

  Multiplexer #(.enable("false"), .width(16)) multiplexer_1 (
    .in0(X), .in1({16{1'b0}}), .out(multiplexer_1_out), .sel(zero_x));
  Multiplexer #(.enable("false"), .width(16)) multiplexer_2 (
    .in0(Y), .in1({16{1'b0}}), .out(multiplexer_2_out), .sel(zero_y));
  Multiplexer #(.enable("false"), .width(16)) multiplexer_3 (
    .in0(multiplexer_1_out), .in1(not_1_out), .out(multiplexer_3_out), .sel(negate_x));
  assign not_1_out = ~multiplexer_1_out;  // NOT_Gate not_1, 16 bits wide
  Multiplexer #(.enable("false"), .width(16)) multiplexer_4 (
    .in0(multiplexer_2_out), .in1(not_2_out), .out(multiplexer_4_out), .sel(negate_y));
  assign not_2_out = ~multiplexer_2_out;  // NOT_Gate not_2, 16 bits wide
  assign and_1_out = multiplexer_3_out & multiplexer_4_out;  // AND_Gate and_1, 16 bits wide
  add16 add16_1 (.A(multiplexer_3_out), .B(multiplexer_4_out), .sum(add16_1_sum), .carry(carry));
  Multiplexer #(.enable("false"), .width(16)) multiplexer_5 (
    .in0(and_1_out), .in1(add16_1_sum), .out(multiplexer_5_out), .sel(add_and));
  Multiplexer #(.enable("false"), .width(16)) multiplexer_6 (
    .in0(multiplexer_5_out), .in1(not_3_out), .out(alu_out), .sel(negate_out));
  assign not_3_out = ~multiplexer_5_out;  // NOT_Gate not_3, 16 bits wide
endmodule

module register1 (
  input  i,
  input  load,
  input  clk,
  input  reset,
  output o
);

  wire multiplexer_1_out;

  Multiplexer #(.enable("false")) multiplexer_1 (.in0(o), .in1(i), .out(multiplexer_1_out), .sel(load));
  D_Flip_Flop d_ff_1 (.D(multiplexer_1_out), .clk(clk), .Q(o), .reset(reset));  // open: Qn, preset
endmodule

module register2 (
  input  [1:0] I,
  input  load,
  input  clk,
  input  reset,
  output [1:0] O
);

  register1 reg0 (.i(I[0]), .load(load), .clk(clk), .reset(reset), .o(O[0]));
  register1 reg1 (.i(I[1]), .load(load), .clk(clk), .reset(reset), .o(O[1]));
endmodule

module register4 (
  input  [3:0] I,
  input  load,
  input  clk,
  input  reset,
  output [3:0] O
);

  register2 reg10 (.O(O[1:0]), .I(I[1:0]), .load(load), .clk(clk), .reset(reset));
  register2 reg32 (.O(O[3:2]), .I(I[3:2]), .load(load), .clk(clk), .reset(reset));
endmodule

module register8 (
  input  [7:0] I,
  input  load,
  input  clk,
  input  reset,
  output [7:0] O
);

  register4 reg3210 (.I(I[3:0]), .load(load), .clk(clk), .reset(reset), .O(O[3:0]));
  register4 reg7654 (.I(I[7:4]), .load(load), .clk(clk), .reset(reset), .O(O[7:4]));
endmodule

module register16 (
  input  [15:0] I,
  input  load,
  input  clk,
  input  reset,
  output [15:0] O
);

  register8 reg7_0 (.I(I[7:0]), .load(load), .clk(clk), .reset(reset), .O(O[7:0]));
  register8 reg15_8 (.I(I[15:8]), .load(load), .clk(clk), .reset(reset), .O(O[15:8]));
endmodule

module RAM8 (
  input  [15:0] I,
  input  load,
  input  clk,
  input  [2:0] address,
  output [15:0] O
);

  wire demultiplexer_1_out0, demultiplexer_1_out1, demultiplexer_1_out2, demultiplexer_1_out3,
       demultiplexer_1_out4, demultiplexer_1_out5, demultiplexer_1_out6, demultiplexer_1_out7,
       demultiplexer_2_out0, demultiplexer_2_out1, demultiplexer_2_out2, demultiplexer_2_out3,
       demultiplexer_2_out4, demultiplexer_2_out5, demultiplexer_2_out6, demultiplexer_2_out7;
  wire [15:0] demultiplexer_3_out0, demultiplexer_3_out1, demultiplexer_3_out2, demultiplexer_3_out3,
       demultiplexer_3_out4, demultiplexer_3_out5, demultiplexer_3_out6, demultiplexer_3_out7, reg0_o,
       reg1_o, reg2_o, reg3_o, reg4_o, reg5_o, reg6_o, reg7_o;

  Demultiplexer #(.enable("false"), .select(3)) demultiplexer_1 (
    .out0(demultiplexer_1_out0), .out1(demultiplexer_1_out1), .out2(demultiplexer_1_out2),
    .out3(demultiplexer_1_out3), .out4(demultiplexer_1_out4), .out5(demultiplexer_1_out5),
    .out6(demultiplexer_1_out6), .out7(demultiplexer_1_out7), .in(clk), .sel(address));
  Demultiplexer #(.enable("false"), .select(3)) demultiplexer_2 (
    .out0(demultiplexer_2_out0), .out1(demultiplexer_2_out1), .out2(demultiplexer_2_out2),
    .out3(demultiplexer_2_out3), .out4(demultiplexer_2_out4), .out5(demultiplexer_2_out5),
    .out6(demultiplexer_2_out6), .out7(demultiplexer_2_out7), .in(load), .sel(address));
  Demultiplexer #(.enable("false"), .select(3), .width(16)) demultiplexer_3 (
    .out0(demultiplexer_3_out0), .out1(demultiplexer_3_out1), .out2(demultiplexer_3_out2),
    .out3(demultiplexer_3_out3), .out4(demultiplexer_3_out4), .out5(demultiplexer_3_out5),
    .out6(demultiplexer_3_out6), .out7(demultiplexer_3_out7), .in(I), .sel(address));
  register16 reg7 (
    .I(demultiplexer_3_out7), .load(demultiplexer_2_out7), .clk(demultiplexer_1_out7), .O(reg7_o));  // open: reset
  register16 reg6 (
    .I(demultiplexer_3_out6), .load(demultiplexer_2_out6), .clk(demultiplexer_1_out6), .O(reg6_o));  // open: reset
  register16 reg5 (
    .I(demultiplexer_3_out5), .load(demultiplexer_2_out5), .clk(demultiplexer_1_out5), .O(reg5_o));  // open: reset
  register16 reg4 (
    .I(demultiplexer_3_out4), .load(demultiplexer_2_out4), .clk(demultiplexer_1_out4), .O(reg4_o));  // open: reset
  register16 reg3 (
    .I(demultiplexer_3_out3), .load(demultiplexer_2_out3), .clk(demultiplexer_1_out3), .O(reg3_o));  // open: reset
  register16 reg2 (
    .I(demultiplexer_3_out2), .load(demultiplexer_2_out2), .clk(demultiplexer_1_out2), .O(reg2_o));  // open: reset
  register16 reg1 (
    .I(demultiplexer_3_out1), .load(demultiplexer_2_out1), .clk(demultiplexer_1_out1), .O(reg1_o));  // open: reset
  register16 reg0 (
    .I(demultiplexer_3_out0), .load(demultiplexer_2_out0), .clk(demultiplexer_1_out0), .O(reg0_o));  // open: reset
  Multiplexer #(.enable("false"), .select(3), .width(16)) multiplexer_1 (
    .in0(reg0_o), .in1(reg1_o), .in2(reg2_o), .in3(reg3_o), .in4(reg4_o), .in5(reg5_o), .in6(reg6_o),
    .in7(reg7_o), .out(O), .sel(address));
endmodule

module RAM64 (
  input  [15:0] I,
  input  load,
  input  clk,
  input  [5:0] address,
  output [15:0] O
);

  wire demultiplexer_2_out0, demultiplexer_2_out1, demultiplexer_2_out2, demultiplexer_2_out3,
       demultiplexer_2_out4, demultiplexer_2_out5, demultiplexer_2_out6, demultiplexer_2_out7,
       demultiplexer_3_out0, demultiplexer_3_out1, demultiplexer_3_out2, demultiplexer_3_out3,
       demultiplexer_3_out4, demultiplexer_3_out5, demultiplexer_3_out6, demultiplexer_3_out7;
  wire [2:0] demultiplexer_1_out0, demultiplexer_1_out1, demultiplexer_1_out2, demultiplexer_1_out3,
       demultiplexer_1_out4, demultiplexer_1_out5, demultiplexer_1_out6, demultiplexer_1_out7;
  wire [15:0] demultiplexer_4_out0, demultiplexer_4_out1, demultiplexer_4_out2, demultiplexer_4_out3,
       demultiplexer_4_out4, demultiplexer_4_out5, demultiplexer_4_out6, demultiplexer_4_out7, ram8_1_o,
       ram8_2_o, ram8_3_o, ram8_4_o, ram8_5_o, ram8_6_o, ram8_7_o, ram8_8_o;

  Demultiplexer #(.enable("false"), .select(3), .width(3)) demultiplexer_1 (
    .out0(demultiplexer_1_out0), .out1(demultiplexer_1_out1), .out2(demultiplexer_1_out2),
    .out3(demultiplexer_1_out3), .out4(demultiplexer_1_out4), .out5(demultiplexer_1_out5),
    .out6(demultiplexer_1_out6), .out7(demultiplexer_1_out7), .in(address[2:0]), .sel(address[5:3]));
  Demultiplexer #(.enable("false"), .select(3)) demultiplexer_2 (
    .out0(demultiplexer_2_out0), .out1(demultiplexer_2_out1), .out2(demultiplexer_2_out2),
    .out3(demultiplexer_2_out3), .out4(demultiplexer_2_out4), .out5(demultiplexer_2_out5),
    .out6(demultiplexer_2_out6), .out7(demultiplexer_2_out7), .in(clk), .sel(address[5:3]));
  Demultiplexer #(.enable("false"), .select(3)) demultiplexer_3 (
    .out0(demultiplexer_3_out0), .out1(demultiplexer_3_out1), .out2(demultiplexer_3_out2),
    .out3(demultiplexer_3_out3), .out4(demultiplexer_3_out4), .out5(demultiplexer_3_out5),
    .out6(demultiplexer_3_out6), .out7(demultiplexer_3_out7), .in(load), .sel(address[5:3]));
  Demultiplexer #(.enable("false"), .select(3), .width(16)) demultiplexer_4 (
    .out0(demultiplexer_4_out0), .out1(demultiplexer_4_out1), .out2(demultiplexer_4_out2),
    .out3(demultiplexer_4_out3), .out4(demultiplexer_4_out4), .out5(demultiplexer_4_out5),
    .out6(demultiplexer_4_out6), .out7(demultiplexer_4_out7), .in(I), .sel(address[5:3]));
  RAM8 ram8_1 (
    .I(demultiplexer_4_out7), .load(demultiplexer_3_out7), .clk(demultiplexer_2_out7),
    .address(demultiplexer_1_out7), .O(ram8_1_o));
  RAM8 ram8_2 (
    .I(demultiplexer_4_out6), .load(demultiplexer_3_out6), .clk(demultiplexer_2_out6),
    .address(demultiplexer_1_out6), .O(ram8_2_o));
  RAM8 ram8_3 (
    .I(demultiplexer_4_out5), .load(demultiplexer_3_out5), .clk(demultiplexer_2_out5),
    .address(demultiplexer_1_out5), .O(ram8_3_o));
  RAM8 ram8_4 (
    .I(demultiplexer_4_out4), .load(demultiplexer_3_out4), .clk(demultiplexer_2_out4),
    .address(demultiplexer_1_out4), .O(ram8_4_o));
  RAM8 ram8_5 (
    .I(demultiplexer_4_out3), .load(demultiplexer_3_out3), .clk(demultiplexer_2_out3),
    .address(demultiplexer_1_out3), .O(ram8_5_o));
  RAM8 ram8_6 (
    .I(demultiplexer_4_out2), .load(demultiplexer_3_out2), .clk(demultiplexer_2_out2),
    .address(demultiplexer_1_out2), .O(ram8_6_o));
  RAM8 ram8_7 (
    .I(demultiplexer_4_out1), .load(demultiplexer_3_out1), .clk(demultiplexer_2_out1),
    .address(demultiplexer_1_out1), .O(ram8_7_o));
  RAM8 ram8_8 (
    .I(demultiplexer_4_out0), .load(demultiplexer_3_out0), .clk(demultiplexer_2_out0),
    .address(demultiplexer_1_out0), .O(ram8_8_o));
  Multiplexer #(.enable("false"), .select(3), .width(16)) multiplexer_1 (
    .in0(ram8_8_o), .in1(ram8_7_o), .in2(ram8_6_o), .in3(ram8_5_o), .in4(ram8_4_o), .in5(ram8_3_o),
    .in6(ram8_2_o), .in7(ram8_1_o), .out(O), .sel(address[5:3]));
endmodule

module RAM512 (
  input  [15:0] I,
  input  load,
  input  clk,
  input  [8:0] address,
  output [15:0] O
);

  wire demultiplexer_2_out0, demultiplexer_2_out1, demultiplexer_2_out2, demultiplexer_2_out3,
       demultiplexer_2_out4, demultiplexer_2_out5, demultiplexer_2_out6, demultiplexer_2_out7,
       demultiplexer_3_out0, demultiplexer_3_out1, demultiplexer_3_out2, demultiplexer_3_out3,
       demultiplexer_3_out4, demultiplexer_3_out5, demultiplexer_3_out6, demultiplexer_3_out7;
  wire [5:0] demultiplexer_1_out0, demultiplexer_1_out1, demultiplexer_1_out2, demultiplexer_1_out3,
       demultiplexer_1_out4, demultiplexer_1_out5, demultiplexer_1_out6, demultiplexer_1_out7;
  wire [15:0] demultiplexer_4_out0, demultiplexer_4_out1, demultiplexer_4_out2, demultiplexer_4_out3,
       demultiplexer_4_out4, demultiplexer_4_out5, demultiplexer_4_out6, demultiplexer_4_out7, ram64_1_o,
       ram64_2_o, ram64_3_o, ram64_4_o, ram64_5_o, ram64_6_o, ram64_7_o, ram64_8_o;

  Demultiplexer #(.enable("false"), .select(3), .width(6)) demultiplexer_1 (
    .out0(demultiplexer_1_out0), .out1(demultiplexer_1_out1), .out2(demultiplexer_1_out2),
    .out3(demultiplexer_1_out3), .out4(demultiplexer_1_out4), .out5(demultiplexer_1_out5),
    .out6(demultiplexer_1_out6), .out7(demultiplexer_1_out7), .in(address[5:0]), .sel(address[8:6]));
  Demultiplexer #(.enable("false"), .select(3)) demultiplexer_2 (
    .out0(demultiplexer_2_out0), .out1(demultiplexer_2_out1), .out2(demultiplexer_2_out2),
    .out3(demultiplexer_2_out3), .out4(demultiplexer_2_out4), .out5(demultiplexer_2_out5),
    .out6(demultiplexer_2_out6), .out7(demultiplexer_2_out7), .in(clk), .sel(address[8:6]));
  Demultiplexer #(.enable("false"), .select(3)) demultiplexer_3 (
    .out0(demultiplexer_3_out0), .out1(demultiplexer_3_out1), .out2(demultiplexer_3_out2),
    .out3(demultiplexer_3_out3), .out4(demultiplexer_3_out4), .out5(demultiplexer_3_out5),
    .out6(demultiplexer_3_out6), .out7(demultiplexer_3_out7), .in(load), .sel(address[8:6]));
  Demultiplexer #(.enable("false"), .select(3), .width(16)) demultiplexer_4 (
    .out0(demultiplexer_4_out0), .out1(demultiplexer_4_out1), .out2(demultiplexer_4_out2),
    .out3(demultiplexer_4_out3), .out4(demultiplexer_4_out4), .out5(demultiplexer_4_out5),
    .out6(demultiplexer_4_out6), .out7(demultiplexer_4_out7), .in(I), .sel(address[8:6]));
  RAM64 ram64_1 (
    .I(demultiplexer_4_out7), .load(demultiplexer_3_out7), .clk(demultiplexer_2_out7),
    .address(demultiplexer_1_out7), .O(ram64_1_o));
  RAM64 ram64_2 (
    .I(demultiplexer_4_out6), .load(demultiplexer_3_out6), .clk(demultiplexer_2_out6),
    .address(demultiplexer_1_out6), .O(ram64_2_o));
  RAM64 ram64_3 (
    .I(demultiplexer_4_out5), .load(demultiplexer_3_out5), .clk(demultiplexer_2_out5),
    .address(demultiplexer_1_out5), .O(ram64_3_o));
  RAM64 ram64_4 (
    .I(demultiplexer_4_out4), .load(demultiplexer_3_out4), .clk(demultiplexer_2_out4),
    .address(demultiplexer_1_out4), .O(ram64_4_o));
  RAM64 ram64_5 (
    .I(demultiplexer_4_out3), .load(demultiplexer_3_out3), .clk(demultiplexer_2_out3),
    .address(demultiplexer_1_out3), .O(ram64_5_o));
  RAM64 ram64_6 (
    .I(demultiplexer_4_out2), .load(demultiplexer_3_out2), .clk(demultiplexer_2_out2),
    .address(demultiplexer_1_out2), .O(ram64_6_o));
  RAM64 ram64_7 (
    .I(demultiplexer_4_out1), .load(demultiplexer_3_out1), .clk(demultiplexer_2_out1),
    .address(demultiplexer_1_out1), .O(ram64_7_o));
  RAM64 ram64_8 (
    .I(demultiplexer_4_out0), .load(demultiplexer_3_out0), .clk(demultiplexer_2_out0),
    .address(demultiplexer_1_out0), .O(ram64_8_o));
  Multiplexer #(.enable("false"), .select(3), .width(16)) multiplexer_1 (
    .in0(ram64_8_o), .in1(ram64_7_o), .in2(ram64_6_o), .in3(ram64_5_o), .in4(ram64_4_o), .in5(ram64_3_o),
    .in6(ram64_2_o), .in7(ram64_1_o), .out(O), .sel(address[8:6]));
endmodule

module RAM4K (
  input  [15:0] I,
  input  load,
  input  clk,
  input  [11:0] address,
  output [15:0] out_5
);

  RAM #(.addrWidth(12), .dataWidth(16)) ram4k (.addr(address), .we(load), .oe(1'b1), .clk(clk), .din(I), .dout(out_5));
endmodule

module RAM16K (
  input  [15:0] I,
  input  load,
  input  clk,
  input  [13:0] address,
  output [15:0] out_5
);

  RAM #(.addrWidth(14), .dataWidth(16)) ram_1 (.addr(address), .we(load), .oe(1'b1), .clk(clk), .din(I), .dout(out_5));
endmodule

module ProgrammCounter (
  input  [15:0] I,
  input  increment,
  input  load,
  input  reset,
  input  clk,
  output [15:0] O
);

  wire [15:0] add16_1_sum, multiplexer_1_out, multiplexer_2_out;

  Multiplexer #(.enable("false"), .width(16)) multiplexer_1 (
    .in0(O), .in1(add16_1_sum), .out(multiplexer_1_out), .sel(increment));
  Multiplexer #(.enable("false"), .width(16)) multiplexer_2 (
    .in0(multiplexer_1_out), .in1(I), .out(multiplexer_2_out), .sel(load));
  add16 add16_1 (.A(O), .B(16'h1), .sum(add16_1_sum));  // open: carry
  register16 count_value (.I(multiplexer_2_out), .load(1'b1), .clk(clk), .reset(reset), .O(O));
endmodule

module CPU (
  input  [15:0] instruction,
  input  [15:0] inM,
  input  reset,
  input  clk,
  output [15:0] outM,
  output writeM,
  output [14:0] addressM,
  output [14:0] pc
);

  wire and_1_out, and_2_out, and_3_out, nor_1_out, not_1_out, or_1_out, or_2_out;
  wire [15:0] D_Register_o, multiplexer_1_out, multiplexer_2_out;
  wire [15:15] A_Register_o, programmcounter_1_o;

  Multiplexer #(.enable("false"), .width(16)) multiplexer_1 (
    .in0(instruction), .in1(outM), .out(multiplexer_1_out), .sel(instruction[15]));
  register16 A_Register (
    .I(multiplexer_1_out), .load(instruction[3]), .clk(clk), .O({A_Register_o[15], addressM}));  // open: reset
  not not_1 (not_1_out, or_2_out);
  nor nor_1 (nor_1_out, outM[15], outM[14], outM[13], outM[12], outM[11], outM[10], outM[9], outM[8], outM[7], outM[6], outM[5], outM[4], outM[3], outM[2], outM[1], outM[0]);
  or or_1 (or_1_out, ~outM[15], outM[14], outM[13], outM[12], outM[11], outM[10], outM[9], outM[8], outM[7], outM[6], outM[5], outM[4], outM[3], outM[2], outM[1], outM[0]);  // OR_Gate
  register16 D_Register (.I(outM), .load(instruction[4]), .clk(clk), .O(D_Register_o));  // open: reset
  Multiplexer #(.enable("false"), .width(16)) multiplexer_2 (
    .in0({A_Register_o[15], addressM}), .in1(inM), .out(multiplexer_2_out), .sel(instruction[12]));
  and and_1 (and_1_out, instruction[2], outM[15]);
  and and_2 (and_2_out, nor_1_out, instruction[1]);
  and and_3 (and_3_out, or_1_out, instruction[0]);
  or or_2 (or_2_out, and_1_out, and_2_out, and_3_out);
  ProgrammCounter programmcounter_1 (
    .I({A_Register_o[15], addressM}), .increment(not_1_out), .load(or_2_out), .reset(reset), .clk(clk),
    .O({programmcounter_1_o[15], pc}));
  ALU alu_1 (
    .X(D_Register_o), .zero_x(instruction[11]), .negate_x(instruction[10]), .Y(multiplexer_2_out),
    .zero_y(instruction[9]), .negate_y(instruction[8]), .add_and(instruction[7]),
    .negate_out(instruction[6]), .alu_out(outM));  // open: carry

  assign writeM = instruction[5];

  // Notes on the sheet:
  //   A-instruction
  //   D-instruction
  //   comp
  //   a or m
  //   jmp
  //   dest
  //   out < 0
  //   out = 0
  //   out > 0
endmodule

module ALU_test (
);

  wire dipswitch_1_p1, dipswitch_1_p2, dipswitch_1_p3, dipswitch_1_p4, dipswitch_1_p5, dipswitch_1_p6;
  wire [3:0] alu_1_alu_out, alu_1_alu_out_2, alu_1_alu_out_3, alu_1_alu_out_4;

  // DipSwitch dipswitch_1: pin names not known; wires that end beside it: dipswitch_1_p1, dipswitch_1_p2, dipswitch_1_p3, dipswitch_1_p4, dipswitch_1_p5, dipswitch_1_p6
  ALU alu_1 (
    .X(16'h101), .zero_x(dipswitch_1_p1), .negate_x(dipswitch_1_p2), .Y({16{1'b1}}), .zero_y(dipswitch_1_p3),
    .negate_y(dipswitch_1_p4), .add_and(dipswitch_1_p5), .negate_out(dipswitch_1_p6),
    .alu_out({alu_1_alu_out_4, alu_1_alu_out_3, alu_1_alu_out_2, alu_1_alu_out}));  // open: carry
  Hex_Digit_Display hex_digit_display_1 (.value(alu_1_alu_out_4));  // open: dp
  Hex_Digit_Display hex_digit_display_2 (.value(alu_1_alu_out_3));  // open: dp
  Hex_Digit_Display hex_digit_display_3 (.value(alu_1_alu_out_2));  // open: dp
  Hex_Digit_Display hex_digit_display_4 (.value(alu_1_alu_out));  // open: dp
endmodule

module screen (
);

  RAM16K ram16k_1 ();  // open: I, load, clk, address, out_5
endmodule

module register_test (
);

  wire button_1_out, button_2_out, button_3_out, clock_1_out, register1_1_o;
  wire [1:0] register2_1_o;
  wire [15:0] dipswitch_1_sw1, register16_1_o;

  DipSwitch #(.number(16)) dipswitch_1 (
    .sw1(dipswitch_1_sw1[0]), .sw2(dipswitch_1_sw1[1]), .sw3(dipswitch_1_sw1[2]), .sw4(dipswitch_1_sw1[3]),
    .sw5(dipswitch_1_sw1[4]), .sw6(dipswitch_1_sw1[5]), .sw7(dipswitch_1_sw1[6]), .sw8(dipswitch_1_sw1[7]),
    .sw9(dipswitch_1_sw1[8]), .sw10(dipswitch_1_sw1[9]), .sw11(dipswitch_1_sw1[10]),
    .sw12(dipswitch_1_sw1[11]), .sw13(dipswitch_1_sw1[12]), .sw14(dipswitch_1_sw1[13]),
    .sw15(dipswitch_1_sw1[14]), .sw16(dipswitch_1_sw1[15]));
  Clock clock_1 (.out(clock_1_out));
  Button button_1 (.out(button_1_out));
  Button button_2 (.out(button_2_out));
  Button button_3 (.out(button_3_out));
  LED led_1 (.in(register1_1_o));
  register1 register1_1 (
    .i(dipswitch_1_sw1[0]), .load(button_1_out), .clk(clock_1_out), .o(register1_1_o));  // open: reset
  register16 register16_1 (
    .I(dipswitch_1_sw1), .load(button_2_out), .clk(clock_1_out), .O(register16_1_o));  // open: reset
  register2 register2_1 (
    .O(register2_1_o), .I(dipswitch_1_sw1[1:0]), .load(button_3_out), .clk(clock_1_out));  // open: reset
  Hex_Digit_Display hex_digit_display_1 (.value(register16_1_o[11:8]));  // open: dp
  Hex_Digit_Display hex_digit_display_2 (.value(register16_1_o[15:12]));  // open: dp
  LED led_2 (.in(register2_1_o[0]));
  LED led_3 (.in(register2_1_o[1]));
  Hex_Digit_Display hex_digit_display_3 (.value(register16_1_o[7:4]));  // open: dp
  Hex_Digit_Display hex_digit_display_4 (.value(register16_1_o[3:0]));  // open: dp
endmodule

module ram_test (
);

  wire button_1_out, clock_1_out;
  wire [5:0] undriven;
  wire [15:0] ram64_1_o, undriven_2;

  // DipSwitch #(.number(6)) dipswitch_1: pin names not known
  // DipSwitch #(.number(16)) dipswitch_2: pin names not known
  Button button_1 (.out(button_1_out));
  Clock clock_1 (.out(clock_1_out));
  RAM64 ram64_1 (.I(undriven_2), .load(button_1_out), .clk(clock_1_out), .address(undriven), .O(ram64_1_o));
  Hex_Digit_Display hex_digit_display_1 (.value(ram64_1_o[15:12]));  // open: dp
  Hex_Digit_Display hex_digit_display_2 (.value(ram64_1_o[11:8]));  // open: dp
  Hex_Digit_Display hex_digit_display_3 (.value(ram64_1_o[7:4]));  // open: dp
  Hex_Digit_Display hex_digit_display_4 (.value(ram64_1_o[3:0]));  // open: dp
endmodule

module ProgrammCounter_test (
);

  wire button_1_out, button_2_out, button_3_out, clock_1_out;
  wire [15:0] programmcounter_1_o;

  Button button_1 (.out(button_1_out));
  Button button_2 (.out(button_2_out));
  Button button_3 (.out(button_3_out));
  Clock clock_1 (.out(clock_1_out));
  ProgrammCounter programmcounter_1 (
    .I(16'h1234), .increment(button_1_out), .load(button_2_out), .reset(button_3_out), .clk(clock_1_out),
    .O(programmcounter_1_o));
  Hex_Digit_Display hex_digit_display_1 (.value(programmcounter_1_o[15:12]));  // open: dp
  Hex_Digit_Display hex_digit_display_2 (.value(programmcounter_1_o[11:8]));  // open: dp
  Hex_Digit_Display hex_digit_display_3 (.value(programmcounter_1_o[7:4]));  // open: dp
  Hex_Digit_Display hex_digit_display_4 (.value(programmcounter_1_o[3:0]));  // open: dp
endmodule

module add16_test (
);

  wire add16_1_carry;
  wire [3:0] add16_1_sum, add16_1_sum_2, add16_1_sum_3, add16_1_sum_4;

  add16 add16_1 (
    .A(16'h1), .B(16'h1), .sum({add16_1_sum_4, add16_1_sum_3, add16_1_sum_2, add16_1_sum}),
    .carry(add16_1_carry));
  LED led_1 (.in(add16_1_carry));
  Hex_Digit_Display hex_digit_display_1 (.value(add16_1_sum_4));  // open: dp
  Hex_Digit_Display hex_digit_display_2 (.value(add16_1_sum_3));  // open: dp
  Hex_Digit_Display hex_digit_display_3 (.value(add16_1_sum_2));  // open: dp
  Hex_Digit_Display hex_digit_display_4 (.value(add16_1_sum));  // open: dp
endmodule
